# Fritzing sketch baby-temp-mon-sketch (saved by Fritzing 0.9.4)
breadboards: 1

parts:
  Pico1 = Raspberry Pi Pico
  Red_LED = LED - 5mm [color="Red (633nm)" package="5 mm [THT]"]
  Green_LED = LED - 5mm [color="Green (555nm)" package="5 mm [THT]"]
  R1 = Resistor [tolerance=±5% resistance=330 package=THT]
  R2 = Resistor [tolerance=±5% resistance=330 package=THT]
  R3 = Resistor [tolerance=±5% resistance=330 package=THT]
  Blue_LED = LED - 5mm [color="Blue (470nm)" package="5 mm [THT]"]

nets:
  N1: Pico1.GND, Red_LED.cathode, Blue_LED.cathode
  N2: Pico1.GP15, R1.Pin_0
  N3: Pico1.GP14, R2.Pin_0
  N4: Pico1.GP13, R3.Pin_0
  N5: Red_LED.anode, R2.Pin_1
  N6: Green_LED.anode, R1.Pin_1
  N7: R3.Pin_1, Blue_LED.anode

custom parts:
  Raspberry Pi Pico: Raspberry Pi Pico. Based around the RP2040 microcontroller the Pico is a low cost microcontroller device bringing Raspberry Pi quality, cost, and easy of use to the microcontroller space.
